# Fritzing sketch lcd (saved by Fritzing 0.9.3b)
breadboards: 1

parts:
  Part1 = Adafruit Feather HUZZAH ESP8266 [part_number="Adafruit #2821"]
  LCD1 = LCD screen
  R1 = Rotary Potentiometer (Small) [maximum_resistance=100kΩ package=THT]
  R2 = Resistor [tolerance=±5% resistance=220 package=THT]

nets:
  N1: Part1.GPIO12/MISO, LCD1.RS
  N2: Part1.GPIO13/MOSI, LCD1.E
  GND: Part1.GND, LCD1.VSS, LCD1.R/W, LCD1.LED-, R1.leg2
  3.3V: Part1.3.3V, LCD1.VDD, R1.leg1, R2.Pin_0
  N3: Part1.GPIO15, LCD1.DB4
  N4: Part1.GPIO16, LCD1.DB5
  N5: Part1.GPIO5/SCL, LCD1.DB6
  N6: Part1.GPIO4/SDA, LCD1.DB7
  N7: LCD1.V0, R1.wiper
  N8: LCD1.LED+, R2.Pin_1

custom parts:
  Adafruit Feather HUZZAH ESP8266: his is the Adafruit Feather HUZZAH ESP8266 - our take on an 'all-in-one' ESP8266 WiFi development board with built in USB and battery charging. Its an ESP8266 WiFi module with all the extras you need, ready to rock! We have other boards in the Feather family, check'em out here. At the Feather HUZZAH's heart is an ESP8266 WiFi microcontroller clocked at 80 MHz and at 3.3V logic. This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
