# Fritzing sketch pwm (saved by Fritzing 0.9.3b)
breadboards: 1

parts:
  Part1 = Adafruit Feather HUZZAH ESP8266 [part_number="Adafruit #2821"]
  PWM1 = PCA9685 16x12-bit PWM Breakout
  LED1 = LED - 3mm [color="Blue (430nm)" package="3 mm [THT]"]
  LED2 = LED - 3mm [color="Blue (430nm)" package="3 mm [THT]"]
  LED3 = LED - 3mm [color="Blue (430nm)" package="3 mm [THT]"]
  LED4 = LED - 3mm [color="Blue (430nm)" package="3 mm [THT]"]
  LED5 = LED - 3mm [color="Blue (430nm)" package="3 mm [THT]"]
  LED6 = LED - 3mm [color="Blue (430nm)" package="3 mm [THT]"]
  LED7 = LED - 3mm [color="Blue (430nm)" package="3 mm [THT]"]
  LED8 = LED - 3mm [color="Blue (430nm)" package="3 mm [THT]"]
  LED9 = LED - 3mm [color="Blue (430nm)" package="3 mm [THT]"]
  LED10 = LED - 3mm [color="Blue (430nm)" package="3 mm [THT]"]
  LED11 = LED - 3mm [color="Blue (430nm)" package="3 mm [THT]"]
  LED12 = LED - 3mm [color="Blue (430nm)" package="3 mm [THT]"]
  LED13 = LED - 3mm [color="Blue (430nm)" package="3 mm [THT]"]
  LED14 = LED - 3mm [color="Blue (430nm)" package="3 mm [THT]"]
  LED15 = LED - 3mm [color="Blue (430nm)" package="3 mm [THT]"]
  LED16 = LED - 3mm [color="Blue (430nm)" package="3 mm [THT]"]
  R1 = Resistor [tolerance=±5% resistance=220 package=THT]
  R2 = Resistor [tolerance=±5% resistance=220 package=THT]
  R3 = Resistor [tolerance=±5% resistance=220 package=THT]
  R4 = Resistor [tolerance=±5% resistance=220 package=THT]
  R5 = Resistor [tolerance=±5% resistance=220 package=THT]
  R6 = Resistor [tolerance=±5% resistance=220 package=THT]
  R7 = Resistor [tolerance=±5% resistance=220 package=THT]
  R8 = Resistor [tolerance=±5% resistance=220 package=THT]
  R9 = Resistor [tolerance=±5% resistance=220 package=THT]
  R10 = Resistor [tolerance=±5% resistance=220 package=THT]
  R11 = Resistor [tolerance=±5% resistance=220 package=THT]
  R12 = Resistor [tolerance=±5% resistance=220 package=THT]
  R13 = Resistor [tolerance=±5% resistance=220 package=THT]
  R14 = Resistor [tolerance=±5% resistance=220 package=THT]
  R15 = Resistor [tolerance=±5% resistance=220 package=THT]
  R16 = Resistor [tolerance=±5% resistance=220 package=THT]

nets:
  N1: Part1.GND, PWM1.no_name_yet#501, PWM1.no_name_yet#1000, LED1.cathode, LED2.cathode, LED3.cathode, LED4.cathode, LED5.cathode, LED6.cathode, LED7.cathode, LED8.cathode, LED9.cathode, LED10.cathode, LED11.cathode, LED12.cathode, LED13.cathode, LED14.cathode, LED15.cathode, LED16.cathode
  N2: Part1.3.3V, PWM1.no_name_yet#505
  N3: Part1.GPIO5/SCL, PWM1.no_name_yet#503
  N4: Part1.GPIO4/SDA, PWM1.no_name_yet#504
  N5: PWM1.no_name_yet#0, R1.Pin_1
  N6: PWM1.no_name_yet#1, R2.Pin_1
  N7: PWM1.no_name_yet#2, R3.Pin_1
  N8: PWM1.no_name_yet#3, R4.Pin_1
  N9: PWM1.no_name_yet#4, R5.Pin_1
  N10: PWM1.no_name_yet#5, R6.Pin_1
  N11: PWM1.no_name_yet#6, R7.Pin_1
  N12: PWM1.no_name_yet#7, R8.Pin_1
  N13: PWM1.no_name_yet#8, R9.Pin_1
  N14: PWM1.no_name_yet#9, R10.Pin_1
  N15: PWM1.no_name_yet#10, R11.Pin_1
  N16: PWM1.no_name_yet#11, R12.Pin_1
  N17: PWM1.no_name_yet#12, R13.Pin_1
  N18: PWM1.no_name_yet#13, R14.Pin_1
  N19: PWM1.no_name_yet#14, R15.Pin_1
  N20: PWM1.no_name_yet#15, R16.Pin_1
  N21: LED1.anode, R1.Pin_0
  N22: LED2.anode, R2.Pin_0
  N23: LED3.anode, R3.Pin_0
  N24: LED4.anode, R4.Pin_0
  N25: LED5.anode, R5.Pin_0
  N26: LED6.anode, R6.Pin_0
  N27: LED7.anode, R7.Pin_0
  N28: LED8.anode, R8.Pin_0
  N29: LED9.anode, R9.Pin_0
  N30: LED10.anode, R10.Pin_0
  N31: LED11.anode, R11.Pin_0
  N32: LED12.anode, R12.Pin_0
  N33: LED13.anode, R13.Pin_0
  N34: LED14.anode, R14.Pin_0
  N35: LED15.anode, R15.Pin_0
  N36: LED16.anode, R16.Pin_0

custom parts:
  Adafruit Feather HUZZAH ESP8266: his is the Adafruit Feather HUZZAH ESP8266 - our take on an 'all-in-one' ESP8266 WiFi development board with built in USB and battery charging. Its an ESP8266 WiFi module with all the extras you need, ready to rock! We have other boards in the Feather family, check'em out here. At the Feather HUZZAH's heart is an ESP8266 WiFi microcontroller clocked at 80 MHz and at 3.3V logic. This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
